# Fritzing sketch main (saved by Fritzing 0.9.5d)
breadboards: 1

parts:
  Part1 = Arduino Uno (Rev3) - ICSP
  FC-1 = Sound Sensor
  Part2 = LCD1602-I2C

nets:
  N1: Part1.A0, FC-1.OUT
  N2: Part1.A4/SDA, Part2.SDA
  N3: Part1.A5/SCL, Part2.SCL
  VCC: Part1.5V, FC-1.VCC, Part2.VCC
  GND: Part1.GND, FC-1.GND, Part2.GND

custom parts:
  LCD1602-I2C: A standard character display, usually with 2x16 characters. Comes in many colors with LCM1602 IIC attached.
