# Fritzing sketch schema (saved by Fritzing 0.9.5d)
breadboards: 1

parts:
  Part1 = Arduino Uno (Rev3) - ICSP
  FC-1 = Sound Sensor
  Part2 = LCD1602-I2C
  LED1 = smd LED [color="Red (633nm)" package="1206 [SMD]"]
  LED2 = smd LED [color="Red (633nm)" package="1206 [SMD]"]
  LED3 = smd LED [color="Red (633nm)" package="1206 [SMD]"]
  R1 = Resistor [tolerance=±5% resistance=220 package="1206 [SMD]"]
  R2 = Resistor [tolerance=±5% resistance=220 package="1206 [SMD]"]
  R3 = Resistor [tolerance=±5% resistance=220 package="1206 [SMD]"]

nets:
  N1: Part1.A0, FC-1.OUT
  N2: Part1.A4/SDA, Part2.SDA
  N3: Part1.A5/SCL, Part2.SCL
  N4: Part1.D9_PWM, R3.Pin_1
  N5: Part1.D10_PWM/SS, R2.Pin_1
  N6: Part1.D11_PWM/MOSI, R1.Pin_1
  VCC: Part1.5V, FC-1.VCC, Part2.VCC
  GND: Part1.GND, FC-1.GND, Part2.GND, LED1.anode, LED2.anode, LED3.anode
  N7: LED1.cathode, R1.Pin_0
  N8: LED2.cathode, R2.Pin_0
  N9: LED3.cathode, R3.Pin_0

custom parts:
  LCD1602-I2C: A standard character display, usually with 2x16 characters. Comes in many colors with LCM1602 IIC attached.
